# Fritzing sketch breadboard (saved by Fritzing 0.9.3b)
breadboards: 1

parts:
  U1 = NodeMCU V1.0
  R1 = Resistor [tolerance=±5% resistance=1k package="1206 [SMD]"]
  S1 = Pushbutton [package="[SMD]"]
  DHT1 = DHT11 Humitidy and Temperature Sensor

nets:
  N1: U1.D1, R1.Pin_1, S1.Pin_1, S1.Pin_2
  N2: U1.D2, DHT1.DATA
  3V3: U1.3V3, R1.Pin_0, DHT1.VDD
  GND: U1.GND, S1.Pin_3, S1.Pin_4, DHT1.GND

custom parts:
  NodeMCU V1.0: ESP8266 based NodeMCU
  DHT11 Humitidy and Temperature Sensor: DHT11 Humidity and Temperature Sensor
